// Digital circuit circuito.dig as structural Verilog
module circuito (
  input  in_1,
  input  b_0,
  input  a_0,
  input  b_1,
  input  a_1,
  input  a_2,
  input  b_2,
  input  a_3,
  input  b_3,
  input  op_0,
  input  op_1,
  input  op_2,
  input  op_3,
  output r_0,
  output c_out,
  output r_1,
  output r_2,
  output r_3
);

  wire and_1_out, and_2_out, and_3_out, and_4_out, and_5_out, and_6_out, and_7_out, and_8_out,
       multiplexer_1_out, multiplexer_3_out, multiplexer_5_out, not_1_out, not_2_out, not_3_out, not_4_out,
       not_5_out, not_6_out, not_7_out, not_8_out, not_9_out, not_10_out, not_11_out, not_12_out, not_13_out,
       not_14_out, not_15_out, not_16_out, or_1_out, or_2_out, or_3_out, or_4_out, or_5_out, or_6_out,
       or_7_out, or_8_out, xor_1_out, xor_2_out, xor_3_out, xor_4_out, xor_5_out, xor_6_out, xor_7_out,
       xor_8_out;

  Multiplexer #(.Selector_Bits(4)) multiplexer_1 (
    .sel({op_0, op_1, op_2, op_3}), .in_0(or_1_out), .in_1(a_0), .in_2(1'b0), .in_3(1'b0), .in_4(1'b0),
    .in_5(1'b0), .in_6(1'b0), .in_7(1'b0), .in_8(1'b0), .in_9(1'b0), .in_10(1'b0), .in_11(1'b0),
    .in_12(1'b0), .in_13(1'b0), .in_14(1'b0), .in_15(1'b0), .out(multiplexer_1_out));
  and and_1 (and_1_out, a_0, b_0);
  not not_1 (not_1_out, and_1_out);
  or or_1 (or_1_out, and_1_out, and_2_out);
  and and_2 (and_2_out, 1'b0, xor_2_out);
  xor xor_1 (xor_1_out, xor_2_out, 1'b0);
  xor xor_2 (xor_2_out, a_0, b_0);
  or or_2 (or_2_out, a_0, b_0);
  not not_2 (not_2_out, or_2_out);
  Multiplexer #(.Selector_Bits(4)) multiplexer_2 (
    .sel({op_3, op_2, op_1, op_0}), .in_0(xor_1_out), .in_1(not_3_out), .in_2(or_2_out), .in_3(not_2_out),
    .in_4(and_1_out), .in_5(not_1_out), .in_6(xor_2_out), .in_7(not_4_out), .in_8(1'b0), .in_9(1'b0),
    .in_10(1'b0), .in_11(1'b0), .in_12(1'b0), .in_13(1'b0), .in_14(1'b0), .in_15(1'b0), .out(r_0));
  not not_3 (not_3_out, xor_2_out);
  not not_4 (not_4_out, a_0);
  Multiplexer #(.Selector_Bits(4)) multiplexer_3 (
    .sel({op_0, op_1, op_2, op_3}), .in_0(or_3_out), .in_1(a_1), .in_2(1'b0), .in_3(1'b0), .in_4(1'b0),
    .in_5(1'b0), .in_6(1'b0), .in_7(1'b0), .in_8(1'b0), .in_9(1'b0), .in_10(1'b0), .in_11(1'b0),
    .in_12(1'b0), .in_13(1'b0), .in_14(1'b0), .in_15(1'b0), .out(multiplexer_3_out));
  and and_3 (and_3_out, a_1, b_1);
  not not_5 (not_5_out, and_3_out);
  or or_3 (or_3_out, and_3_out, and_4_out);
  and and_4 (and_4_out, multiplexer_1_out, xor_4_out);
  xor xor_3 (xor_3_out, xor_4_out, multiplexer_1_out);
  xor xor_4 (xor_4_out, a_1, b_1);
  or or_4 (or_4_out, a_1, b_1);
  not not_6 (not_6_out, or_4_out);
  Multiplexer #(.Selector_Bits(4)) multiplexer_4 (
    .sel({op_3, op_2, op_1, op_0}), .in_0(xor_3_out), .in_1(not_7_out), .in_2(or_4_out), .in_3(not_6_out),
    .in_4(and_3_out), .in_5(not_5_out), .in_6(xor_4_out), .in_7(not_8_out), .in_8(multiplexer_1_out),
    .in_9(1'b0), .in_10(1'b0), .in_11(1'b0), .in_12(1'b0), .in_13(1'b0), .in_14(1'b0), .in_15(1'b0), .out(r_1));
  not not_7 (not_7_out, xor_4_out);
  not not_8 (not_8_out, a_1);
  Multiplexer #(.Selector_Bits(4)) multiplexer_5 (
    .sel({op_0, op_1, op_2, op_3}), .in_0(or_5_out), .in_1(a_2), .in_2(1'b0), .in_3(1'b0), .in_4(1'b0),
    .in_5(1'b0), .in_6(1'b0), .in_7(1'b0), .in_8(1'b0), .in_9(1'b0), .in_10(1'b0), .in_11(1'b0),
    .in_12(1'b0), .in_13(1'b0), .in_14(1'b0), .in_15(1'b0), .out(multiplexer_5_out));
  and and_5 (and_5_out, a_2, b_2);
  not not_9 (not_9_out, and_5_out);
  or or_5 (or_5_out, and_5_out, and_6_out);
  and and_6 (and_6_out, multiplexer_3_out, xor_6_out);
  xor xor_5 (xor_5_out, xor_6_out, multiplexer_3_out);
  xor xor_6 (xor_6_out, a_2, b_2);
  not not_10 (not_10_out, or_6_out);
  or or_6 (or_6_out, a_2, b_2);
  Multiplexer #(.Selector_Bits(4)) multiplexer_6 (
    .sel({op_3, op_2, op_1, op_0}), .in_0(xor_5_out), .in_1(not_11_out), .in_2(or_6_out), .in_3(not_10_out),
    .in_4(and_5_out), .in_5(not_9_out), .in_6(xor_6_out), .in_7(not_12_out), .in_8(multiplexer_3_out),
    .in_9(1'b0), .in_10(1'b0), .in_11(1'b0), .in_12(1'b0), .in_13(1'b0), .in_14(1'b0), .in_15(1'b0), .out(r_2));
  not not_11 (not_11_out, xor_6_out);
  not not_12 (not_12_out, a_2);
  Multiplexer #(.Selector_Bits(4)) multiplexer_7 (
    .sel({op_0, op_1, op_2, op_3}), .in_0(or_7_out), .in_1(a_3), .in_2(1'b0), .in_3(1'b0), .in_4(1'b0),
    .in_5(1'b0), .in_6(1'b0), .in_7(1'b0), .in_8(1'b0), .in_9(1'b0), .in_10(1'b0), .in_11(1'b0),
    .in_12(1'b0), .in_13(1'b0), .in_14(1'b0), .in_15(1'b0), .out(c_out));
  or or_7 (or_7_out, and_7_out, and_8_out);
  and and_7 (and_7_out, a_3, b_3);
  not not_13 (not_13_out, and_7_out);
  and and_8 (and_8_out, multiplexer_5_out, xor_7_out);
  xor xor_7 (xor_7_out, a_3, b_3);
  xor xor_8 (xor_8_out, xor_7_out, multiplexer_5_out);
  or or_8 (or_8_out, a_3, b_3);
  not not_14 (not_14_out, or_8_out);
  Multiplexer #(.Selector_Bits(4)) multiplexer_8 (
    .sel({op_3, op_2, op_1, op_0}), .in_0(xor_8_out), .in_1(not_15_out), .in_2(or_8_out), .in_3(not_14_out),
    .in_4(and_7_out), .in_5(not_13_out), .in_6(xor_7_out), .in_7(not_16_out), .in_8(multiplexer_5_out),
    .in_9(1'b0), .in_10(1'b0), .in_11(1'b0), .in_12(1'b0), .in_13(1'b0), .in_14(1'b0), .in_15(1'b0), .out(r_3));
  not not_15 (not_15_out, xor_7_out);
  not not_16 (not_16_out, a_3);
endmodule
